// Logisim project Dflipflop.circ as structural Verilog: 1 circuit, main circuit Dflipflop
module Dflipflop (
  input  CLOCK,
  input  Write,
  input  D,
  input  RESET,
  output val
);

  wire and_1_out, nand_1_out, nand_2_out, nand_3_out, nand_4_out, nand_5_out, nand_6_out, nand_7_out,
       nand_8_out, nand_9_out, nand_11_out, not_1_out, not_2_out, not_3_out, not_4_out, not_5_out, undriven,
       undriven_2, undriven_3, undriven_4, undriven_5, undriven_6, undriven_7, undriven_8;

  not not_1 (not_1_out, undriven_3);
  not not_2 (not_2_out, RESET);
  not not_3 (not_3_out, undriven);
  nand nand_1 (nand_1_out, Write, D);
  nand nand_2 (nand_2_out, not_1_out, undriven_8);
  nand nand_3 (nand_3_out, nand_1_out, nand_2_out);
  and and_1 (and_1_out, nand_3_out, not_2_out);
  not not_4 (not_4_out, undriven_5);
  nand nand_4 (nand_4_out, undriven_4, and_1_out);
  nand nand_5 (nand_5_out, not_3_out, not_4_out);
  nand nand_6 (nand_6_out, nand_4_out, nand_7_out);
  nand nand_7 (nand_7_out, nand_5_out, undriven_6);
  not not_5 (not_5_out, undriven_7);
  nand nand_8 (nand_8_out, undriven_2, nand_6_out);
  nand nand_9 (nand_9_out, CLOCK, not_5_out);
  nand nand_10 (val, nand_8_out, nand_11_out);
  nand nand_11 (nand_11_out, nand_9_out, undriven_8);
endmodule
