// Logisim project FinalCircuit.circ as structural Verilog: 19 circuits, main circuit ALUForge
module ALUForge (
  input  Start
);

  wire A_S, ACC_S, B_S, clock_1_out, decode_1_sign_out, decode_1_w_a, decode_1_w_acc, decode_1_w_b,
       decode_1_w_rem, decode_1_w_res, REM_S, RES_S;
  wire [7:0] A_V, ACC_V, B_V, decode_1_data_out, ins_fetch_and_pc_1_addr_out, REM_V, RES_V;
  wire [15:0] ins_fetch_and_pc_1_ins_out, rom_1_data;

  ROM #(.dataWidth(16)) rom_1 (.addr(ins_fetch_and_pc_1_addr_out), .data(rom_1_data));
  Clock clock_1 (.out(clock_1_out));
  decode decode_1 (
    .INST_IN(ins_fetch_and_pc_1_ins_out), .ACC_IN(A_V), .A_IN(ACC_V), .B_IN(B_V), .REM_IN(REM_V),
    .RES_IN(RES_V), .ACC_SIGN(A_S), .A_SIGN(ACC_S), .B_SIGN(B_S), .REM_SIGN(REM_S), .RES_SIGN(RES_S),
    .W_ACC(decode_1_w_acc), .W_B(decode_1_w_b), .W_A(decode_1_w_a), .DATA_OUT(decode_1_data_out),
    .W_REM(decode_1_w_rem), .W_RES(decode_1_w_res), .SIGN_OUT(decode_1_sign_out));  // open: END_INST
  Ins_fetch_and_pc ins_fetch_and_pc_1 (
    .Clock(clock_1_out), .INS_IN(rom_1_data), .RESET(Start), .INS_OUT(ins_fetch_and_pc_1_ins_out),
    .ADDR_OUT(ins_fetch_and_pc_1_addr_out));  // open: NO_CYCLES
  LedBar ledbar_1 (
    .led0(ACC_V[7]), .led1(ACC_V[6]), .led2(ACC_V[5]), .led3(ACC_V[4]), .led4(ACC_V[3]), .led5(ACC_V[2]),
    .led6(ACC_V[1]), .led7(ACC_V[0]));
  // registor A: pin names not known; wires that end beside it: clock_1_out, decode_1_w_a, decode_1_data_out, decode_1_sign_out, Start, A_V, A_S
  registor ACC (
    .CLOCK(clock_1_out), .WRITE(decode_1_w_acc), .Data_in(decode_1_data_out), .Sign(decode_1_sign_out),
    .RESET(Start), .data_out(ACC_V), .Sign_out(ACC_S));
  registor B (
    .CLOCK(clock_1_out), .WRITE(decode_1_w_b), .Data_in(decode_1_data_out), .Sign(decode_1_sign_out),
    .RESET(Start), .data_out(B_V), .Sign_out(B_S));
  registor Remainder (
    .CLOCK(clock_1_out), .WRITE(decode_1_w_rem), .Data_in(decode_1_data_out), .Sign(decode_1_sign_out),
    .RESET(Start), .data_out(REM_V), .Sign_out(REM_S));
  registor Result (
    .CLOCK(clock_1_out), .WRITE(decode_1_w_res), .Data_in(decode_1_data_out), .Sign(decode_1_sign_out),
    .RESET(Start), .data_out(RES_V), .Sign_out(RES_S));

  // Other names for the same wires on the sheet: RESET = Start

  // Notes on the sheet:
  //   contents of rom_1 (hex, n*v repeats v):
  //   3202 0 0 502 a02
  //   000=END 001=MOV 010=LOAD 011=SUM 100=MUL 101=DIV
endmodule

module registor (
  input  CLOCK,
  input  WRITE,
  input  [7:0] Data_in,
  input  Sign,
  input  RESET,
  output [7:0] data_out,
  output Sign_out
);

  Dflipflop C1 (.CLOCK(CLOCK), .Write(WRITE), .D(Data_in[0]), .RESET(RESET), .val(data_out[0]));
  Dflipflop C2 (.CLOCK(CLOCK), .Write(WRITE), .D(Data_in[1]), .RESET(RESET), .val(data_out[1]));
  Dflipflop C3 (.CLOCK(CLOCK), .Write(WRITE), .D(Data_in[2]), .RESET(RESET), .val(data_out[2]));
  Dflipflop C4 (.CLOCK(CLOCK), .Write(WRITE), .D(Data_in[3]), .RESET(RESET), .val(data_out[3]));
  Dflipflop C5 (.CLOCK(CLOCK), .Write(WRITE), .D(Data_in[4]), .RESET(RESET), .val(data_out[4]));
  Dflipflop C6 (.CLOCK(CLOCK), .Write(WRITE), .D(Data_in[5]), .RESET(RESET), .val(data_out[5]));
  Dflipflop C7 (.CLOCK(CLOCK), .Write(WRITE), .D(Data_in[6]), .RESET(RESET), .val(data_out[6]));
  Dflipflop C8 (.CLOCK(CLOCK), .Write(WRITE), .D(Data_in[7]), .RESET(RESET), .val(data_out[7]));
  Dflipflop dflipflop_1 (.CLOCK(CLOCK), .Write(WRITE), .D(Sign), .RESET(RESET), .val(Sign_out));
endmodule

module Dflipflop (
  input  CLOCK,
  input  Write,
  input  D,
  input  RESET,
  output val
);

  wire and_1_out, nand_1_out, nand_2_out, nand_3_out, nand_4_out, nand_5_out, nand_6_out, nand_7_out,
       nand_8_out, nand_9_out, nand_11_out, not_1_out, not_2_out, not_3_out, not_4_out, not_5_out;

  not not_1 (not_1_out, Write);
  not not_2 (not_2_out, RESET);
  nand nand_1 (nand_1_out, Write, D);
  nand nand_2 (nand_2_out, not_1_out, val);
  nand nand_3 (nand_3_out, nand_1_out, nand_2_out);
  and and_1 (and_1_out, nand_3_out, not_2_out);
  not not_3 (not_3_out, CLOCK);
  not not_4 (not_4_out, and_1_out);
  nand nand_4 (nand_4_out, and_1_out, not_3_out);
  nand nand_5 (nand_5_out, not_3_out, not_4_out);
  nand nand_6 (nand_6_out, nand_4_out, nand_7_out);
  nand nand_7 (nand_7_out, nand_6_out, nand_5_out);
  not not_5 (not_5_out, nand_6_out);
  nand nand_8 (nand_8_out, nand_6_out, CLOCK);
  nand nand_9 (nand_9_out, CLOCK, not_5_out);
  nand nand_10 (val, nand_8_out, nand_11_out);
  nand nand_11 (nand_11_out, val, nand_9_out);
endmodule

module ADD_full (
  input  A,
  input  B,
  input  Cin,
  output Sum,
  output Cout
);

  Multiplexer #(.enable("true"), .select(3)) multiplexer_1 (
    .in0(1'b0), .in1(1'b1), .in2(1'b1), .in3(1'b0), .in4(1'b1), .in5(1'b0), .in6(1'b0), .in7(1'b1),
    .out(Sum), .sel({A, B, Cin}));  // open: en
  Multiplexer #(.enable("true"), .select(3)) multiplexer_2 (
    .in0(1'b0), .in1(1'b0), .in2(1'b0), .in3(1'b1), .in4(1'b0), .in5(1'b1), .in6(1'b1), .in7(1'b1),
    .out(Cout), .sel({A, B, Cin}));  // open: en
endmodule

module ADD (
  input  Cin,
  input  [7:0] A,
  input  [7:0] B,
  output [7:0] Sum,
  output Cout
);

  wire add_full_1_cout, add_full_2_cout, add_full_3_cout, add_full_4_cout, add_full_5_cout, add_full_6_cout,
       add_full_7_cout;

  ADD_full add_full_1 (.A(A[0]), .B(B[0]), .Cin(Cin), .Sum(Sum[0]), .Cout(add_full_1_cout));
  ADD_full add_full_2 (.A(A[1]), .B(B[1]), .Cin(add_full_1_cout), .Sum(Sum[1]), .Cout(add_full_2_cout));
  ADD_full add_full_3 (.A(A[2]), .B(B[2]), .Cin(add_full_2_cout), .Sum(Sum[2]), .Cout(add_full_3_cout));
  ADD_full add_full_4 (.A(A[3]), .B(B[3]), .Cin(add_full_3_cout), .Sum(Sum[3]), .Cout(add_full_4_cout));
  ADD_full add_full_5 (.A(A[4]), .B(B[4]), .Cin(add_full_4_cout), .Sum(Sum[4]), .Cout(add_full_5_cout));
  ADD_full add_full_6 (.A(A[5]), .B(B[5]), .Cin(add_full_5_cout), .Sum(Sum[5]), .Cout(add_full_6_cout));
  ADD_full add_full_7 (.A(A[6]), .B(B[6]), .Cin(add_full_6_cout), .Sum(Sum[6]), .Cout(add_full_7_cout));
  ADD_full add_full_8 (.A(A[7]), .B(B[7]), .Cin(add_full_7_cout), .Sum(Sum[7]), .Cout(Cout));
endmodule

module SUM (
  input  [7:0] A,
  input  [7:0] B,
  input  A_sign,
  input  B_sign,
  output [7:0] out_5,
  output S9
);

  wire AminusB_cout, BminusA_cout, not_3_out, not_4_out;
  wire [7:0] AminusB_sum, APlusB_sum, BminusA_sum, multiplexer_1_out, multiplexer_2_out, not_1_out,
       not_2_out, rcomp_1_comp, rcomp_2_comp;

  assign not_1_out = ~A;  // NOT_Gate not_1, 8 bits wide
  assign not_2_out = ~B;  // NOT_Gate not_2, 8 bits wide
  ADD APlusB (.Cin(1'b0), .A(A), .B(B), .Sum(APlusB_sum));  // open: Cout
  ADD BminusA (.Cin(1'b1), .A(not_1_out), .B(B), .Sum(BminusA_sum), .Cout(BminusA_cout));
  ADD AminusB (.Cin(1'b1), .A(A), .B(not_2_out), .Sum(AminusB_sum), .Cout(AminusB_cout));
  Multiplexer #(.width(8)) multiplexer_1 (
    .in0(rcomp_1_comp), .in1(BminusA_sum), .out(multiplexer_1_out), .sel(BminusA_cout));
  not not_3 (not_3_out, BminusA_cout);
  Multiplexer #(.width(8)) multiplexer_2 (
    .in0(rcomp_2_comp), .in1(AminusB_sum), .out(multiplexer_2_out), .sel(AminusB_cout));
  Rcomp rcomp_1 (.Num(BminusA_sum), .comp(rcomp_1_comp));
  not not_4 (not_4_out, AminusB_cout);
  Multiplexer #(.select(2), .width(8)) multiplexer_3 (
    .in0(APlusB_sum), .in1(multiplexer_2_out), .in2(multiplexer_1_out), .in3(APlusB_sum), .out(out_5),
    .sel({B_sign, A_sign}));
  Multiplexer #(.select(2)) multiplexer_4 (
    .in0(1'b0), .in1(not_4_out), .in2(not_3_out), .in3(1'b1), .out(S9), .sel({B_sign, A_sign}));
  Rcomp rcomp_2 (.Num(AminusB_sum), .comp(rcomp_2_comp));
endmodule

module Rcomp (
  input  [7:0] Num,
  output [7:0] comp
);

  wire [7:0] not_1_out;

  assign not_1_out = ~Num;  // NOT_Gate not_1, 8 bits wide
  ADD add_1 (.Cin(1'b0), .A(8'h1), .B(not_1_out), .Sum(comp));  // open: Cout
endmodule

module decode (
  input  [15:0] INST_IN,
  input  [7:0] ACC_IN,
  input  [7:0] A_IN,
  input  [7:0] B_IN,
  input  [7:0] REM_IN,
  input  [7:0] RES_IN,
  input  ACC_SIGN,
  input  A_SIGN,
  input  B_SIGN,
  input  REM_SIGN,
  input  RES_SIGN,
  output END_INST,
  output W_ACC,
  output W_B,
  output W_A,
  output [7:0] DATA_OUT,
  output W_REM,
  output W_RES,
  output SIGN_OUT
);

  wire decoder_1_out1, decoder_1_out2, load_1_sign_out, load_1_write_a, load_1_write_acc, load_1_write_b,
       load_1_write_rem, load_1_write_res, move_1_write_a, move_1_write_acc, move_1_write_b,
       move_1_write_rem, move_1_write_res, MOVE_SIGN;
  wire [7:0] load_1_data_out, move_1_data_out;

  Decoder #(.select(3)) decoder_1 (
    .out0(END_INST), .out1(decoder_1_out1), .out2(decoder_1_out2), .sel(INST_IN[2:0]));  // open: out3, out4, out5, out6, out7, en
  Multiplexer #(.select(3)) multiplexer_1 (
    .in0(ACC_SIGN), .in1(A_SIGN), .in2(B_SIGN), .in3(REM_SIGN), .in4(RES_SIGN), .in5(1'b0), .in6(1'b0),
    .in7(1'b0), .out(MOVE_SIGN), .sel(INST_IN[8:6]));
  Move move_1 (
    .ENABLE(decoder_1_out1), .DST(INST_IN[5:3]), .SRC(INST_IN[8:6]), .ACC_IN(ACC_IN), .A_IN(A_IN),
    .B_IN(B_IN), .REM_IN(REM_IN), .RES_IN(RES_IN), .WRITE_ACC(move_1_write_acc), .WRITE_A(move_1_write_a),
    .WRITE_B(move_1_write_b), .WRITE_REM(move_1_write_rem), .WRITE_RES(move_1_write_res),
    .DATA_OUT(move_1_data_out));
  LOAD load_1 (
    .Enable(decoder_1_out2), .ADDR(INST_IN[5:3]), .VALUE_IN(INST_IN[14:6]), .WRITE_ACC(load_1_write_acc),
    .WRITE_A(load_1_write_a), .WRITE_B(load_1_write_b), .WRITE_REM(load_1_write_rem),
    .WRITE_RES(load_1_write_res), .DATA_OUT(load_1_data_out), .SIGN_OUT(load_1_sign_out));
  or or_1 (W_REM, move_1_write_rem, load_1_write_rem);
  or or_2 (W_RES, load_1_write_res, move_1_write_res);
  or or_3 (W_ACC, move_1_write_acc, load_1_write_acc);
  buf or_4 (W_B, load_1_write_b);  // OR_Gate
  or or_5 (W_A, move_1_write_a, load_1_write_a);
  Multiplexer #(.select(3), .width(8)) multiplexer_2 (
    .in1(move_1_data_out), .in2(load_1_data_out), .out(DATA_OUT), .sel(INST_IN[2:0]));  // open: in0, in3, in4, in5, in6, in7
  Multiplexer #(.select(3)) multiplexer_3 (
    .in1(MOVE_SIGN), .in2(load_1_sign_out), .out(SIGN_OUT), .sel(INST_IN[2:0]));  // open: in0, in3, in4, in5, in6, in7

  // Other names for the same wires on the sheet: A_S = A_SIGN; A_V[7:0] = A_IN; ACC_S = ACC_SIGN; ACC_V[7:0] = ACC_IN;
  //   B_S = B_SIGN; B_V[7:0] = B_IN; SRC3[2:0] = INST_IN[8:6]; REM_S = REM_SIGN; REM_V[7:0] = REM_IN;
  //   RES_S = RES_SIGN; RES_V[7:0] = RES_IN

  // Notes on the sheet:
  //   Free decoder outputs: 011=SUM  100=MUL  101=DIV
  //   Sign of MOV source register (selected by SRC)
  //   Register values as tunnels: ACC_V A_V B_V REM_V RES_V and signs ACC_S A_S B_S REM_S RES_S
  //   Each OR gate has 3 FREE inputs: connect SUM / MUL / DIV write signals here
  //   DATA mux + SIGN mux: inputs 3,4,5 FREE for SUM, MUL, DIV
endmodule

module div_circuit (
  input  [7:0] A,
  input  [7:0] B,
  output [7:0] Quotient,
  output [7:0] Reminder,
  output Error
);

  wire comparator_1_lt, subtractor_1_bout, subtractor_2_bout, subtractor_3_bout, subtractor_4_bout,
       subtractor_5_bout, subtractor_6_bout, subtractor_7_bout, subtractor_8_bout, zero8_2_output,
       zero8_3_output, zero8_4_output, zero8_5_output, zero8_6_output, zero8_7_output, zero8_8_output,
       zero8_9_output;
  wire [1:0] pull_resistor_1_node_2;
  wire [5:0] pull_resistor_1_node;
  wire [7:0] and_8_out, multiplexer_1_out, multiplexer_2_out, multiplexer_3_out, multiplexer_4_out,
       multiplexer_6_out, multiplexer_7_out, multiplexer_8_out, subtractor_1_out, subtractor_2_out,
       subtractor_3_out, subtractor_4_out, subtractor_5_out, subtractor_6_out, subtractor_7_out,
       subtractor_8_out;

  Pull_Resistor pull_resistor_1 (.node({pull_resistor_1_node_2, pull_resistor_1_node}));
  Zero8 zero8_1 (.A(B), .Output(Error));
  Comparator #(.mode("unsigned")) comparator_1 (.a(A), .b(B), .lt(comparator_1_lt));  // open: gt, eq
  Subtractor subtractor_1 (
    .a(A), .b({B[0], pull_resistor_1_node_2, pull_resistor_1_node[5:1]}), .out(subtractor_1_out),
    .bout(subtractor_1_bout));  // open: bin
  and and_1 (and_8_out[7], ~subtractor_1_bout, zero8_2_output);  // AND_Gate
  Zero8 zero8_2 (.A({1'b0, B[7:1]}), .Output(zero8_2_output));
  Multiplexer #(.width(8)) multiplexer_1 (.in0(A), .in1(subtractor_1_out), .out(multiplexer_1_out), .sel(and_8_out[7]));
  Subtractor subtractor_2 (
    .a(multiplexer_1_out), .b({B[1:0], pull_resistor_1_node_2, pull_resistor_1_node[5:2]}),
    .out(subtractor_2_out), .bout(subtractor_2_bout));  // open: bin
  and and_2 (and_8_out[6], ~subtractor_2_bout, zero8_3_output);  // AND_Gate
  Zero8 zero8_3 (.A({2'b00, B[7:2]}), .Output(zero8_3_output));
  Multiplexer #(.width(8)) multiplexer_2 (
    .in0(multiplexer_1_out), .in1(subtractor_2_out), .out(multiplexer_2_out), .sel(and_8_out[6]));
  Subtractor subtractor_3 (
    .a(multiplexer_2_out), .b({B[2:0], pull_resistor_1_node_2, pull_resistor_1_node[5:3]}),
    .out(subtractor_3_out), .bout(subtractor_3_bout));  // open: bin
  and and_3 (and_8_out[5], ~subtractor_3_bout, zero8_4_output);  // AND_Gate
  Zero8 zero8_4 (.A({3'b000, B[7:3]}), .Output(zero8_4_output));
  Multiplexer #(.width(8)) multiplexer_3 (
    .in0(multiplexer_2_out), .in1(subtractor_3_out), .out(multiplexer_3_out), .sel(and_8_out[5]));
  Subtractor subtractor_4 (
    .a(multiplexer_3_out), .b({B[3:0], pull_resistor_1_node_2, pull_resistor_1_node[5:4]}),
    .out(subtractor_4_out), .bout(subtractor_4_bout));  // open: bin
  and and_4 (and_8_out[4], ~subtractor_4_bout, zero8_5_output);  // AND_Gate
  Zero8 zero8_5 (.A({4'b0000, B[7:4]}), .Output(zero8_5_output));
  Multiplexer #(.width(8)) multiplexer_4 (
    .in0(multiplexer_3_out), .in1(subtractor_4_out), .out(multiplexer_4_out), .sel(and_8_out[4]));
  Subtractor subtractor_5 (
    .a(multiplexer_4_out), .b({B[4:0], pull_resistor_1_node_2, pull_resistor_1_node[5]}),
    .out(subtractor_5_out), .bout(subtractor_5_bout));  // open: bin
  Zero8 zero8_6 (.A({{5{1'b0}}, B[7:5]}), .Output(zero8_6_output));
  Multiplexer #(.width(8)) multiplexer_5 (.in0(and_8_out), .out(Quotient), .sel(comparator_1_lt));  // open: in1
  and and_5 (and_8_out[3], ~subtractor_5_bout, zero8_6_output);  // AND_Gate
  Multiplexer #(.width(8)) multiplexer_6 (
    .in0(multiplexer_4_out), .in1(subtractor_5_out), .out(multiplexer_6_out), .sel(and_8_out[3]));
  Subtractor subtractor_6 (
    .a(multiplexer_6_out), .b({B[5:0], pull_resistor_1_node_2}), .out(subtractor_6_out),
    .bout(subtractor_6_bout));  // open: bin
  Zero8 zero8_7 (.A({{6{1'b0}}, B[7:6]}), .Output(zero8_7_output));
  and and_6 (and_8_out[2], ~subtractor_6_bout, zero8_7_output);  // AND_Gate
  Multiplexer #(.width(8)) multiplexer_7 (
    .in0(multiplexer_6_out), .in1(subtractor_6_out), .out(multiplexer_7_out), .sel(and_8_out[2]));
  Zero8 zero8_8 (.A({{7{1'b0}}, B[7]}), .Output(zero8_8_output));
  Subtractor subtractor_7 (
    .a(multiplexer_7_out), .b({B[6:0], pull_resistor_1_node_2[1]}), .out(subtractor_7_out),
    .bout(subtractor_7_bout));  // open: bin
  and and_7 (and_8_out[1], ~subtractor_7_bout, zero8_8_output);  // AND_Gate
  Multiplexer #(.width(8)) multiplexer_8 (
    .in0(multiplexer_7_out), .in1(subtractor_7_out), .out(multiplexer_8_out), .sel(and_8_out[1]));
  Zero8 zero8_9 (.A({8{1'b0}}), .Output(zero8_9_output));
  Subtractor subtractor_8 (
    .a(multiplexer_8_out), .b(B), .out(subtractor_8_out), .bout(subtractor_8_bout));  // open: bin
  and and_8 (and_8_out[0], ~subtractor_8_bout, zero8_9_output);  // AND_Gate
  Multiplexer #(.width(8)) multiplexer_9 (
    .in0(multiplexer_8_out), .in1(subtractor_8_out), .out(Reminder), .sel(and_8_out[0]));
endmodule

module DIV (
  input  [7:0] A,
  input  [7:0] B,
  input  A_sign,
  input  B_sign,
  output [7:0] Reminder,
  output Sign,
  output Zero_Error,
  output [7:0] Quotient
);

  wire [7:0] div_circuit_1_quotient, div_circuit_1_reminder;

  div_circuit div_circuit_1 (
    .A(A), .B(B), .Quotient(div_circuit_1_quotient), .Reminder(div_circuit_1_reminder), .Error(Zero_Error));
  xor xor_1 (Sign, A_sign, B_sign);
  Multiplexer #(.width(8)) multiplexer_1 (
    .in0(div_circuit_1_reminder), .in1({8{1'b0}}), .out(Reminder), .sel(Zero_Error));
  Multiplexer #(.width(8)) multiplexer_2 (
    .in0(div_circuit_1_quotient), .in1({8{1'b0}}), .out(Quotient), .sel(Zero_Error));
endmodule

// Z8
module Zero8 (
  input  [7:0] A,
  output Output
);

  wire or_1_out, or_2_out, or_3_out, or_4_out, or_5_out, or_6_out;

  or or_1 (or_1_out, A[0], A[1]);
  or or_2 (or_2_out, A[2], A[3]);
  or or_3 (or_3_out, A[4], A[5]);
  or or_4 (or_4_out, A[6], A[7]);
  or or_5 (or_5_out, or_1_out, or_2_out);
  nor nor_1 (Output, or_5_out, or_6_out);
  or or_6 (or_6_out, or_3_out, or_4_out);
endmodule

module IR (
  input  CLOCK,
  input  WRITE,
  input  [15:0] INS_IN,
  output [15:0] INS_OUT
);

  registor registor_1 (
    .CLOCK(CLOCK), .WRITE(WRITE), .Data_in(INS_IN[7:0]), .Sign(1'b0), .RESET(1'b0), .data_out(INS_OUT[7:0]));  // open: Sign_out
  registor registor_2 (
    .CLOCK(CLOCK), .WRITE(WRITE), .Data_in(INS_IN[15:8]), .Sign(1'b0), .RESET(1'b0), .data_out(INS_OUT[15:8]));  // open: Sign_out
endmodule

module Ins_fetch_and_pc (
  input  Clock,
  input  [15:0] INS_IN,
  input  RESET,
  output [15:0] INS_OUT,
  output [7:0] ADDR_OUT,
  output [7:0] NO_CYCLES
);

  wire not_1_out;
  wire [7:0] add_1_sum;

  not not_1 (not_1_out, Clock);
  TICKER ticker_1 (.Clock(Clock), .RESET(RESET), .Tick(NO_CYCLES));
  IR ir_1 (.CLOCK(Clock), .WRITE(1'b1), .INS_IN(INS_IN), .INS_OUT(INS_OUT));
  registor PC (
    .CLOCK(not_1_out), .WRITE(1'b1), .Data_in(add_1_sum), .Sign(1'b0), .RESET(RESET), .data_out(ADDR_OUT));  // open: Sign_out
  ADD add_1 (.Cin(1'b1), .A(ADDR_OUT), .B({8{1'b0}}), .Sum(add_1_sum));  // open: Cout
endmodule

module TICKER (
  input  Clock,
  input  RESET,
  output [7:0] Tick
);

  wire [7:0] add_1_sum;

  ADD add_1 (.Cin(1'b1), .A({8{1'b0}}), .B(Tick), .Sum(add_1_sum));  // open: Cout
  registor registor_1 (
    .CLOCK(Clock), .WRITE(1'b1), .Data_in(add_1_sum), .Sign(1'b0), .RESET(RESET), .data_out(Tick));  // open: Sign_out
endmodule

module CELL (
  input  a,
  input  b,
  input  acc,
  input  cin,
  output a_out,
  output cout,
  output s
);

  wire and_1_out, and_2_out, and_3_out, xor_1_out;

  and and_1 (and_1_out, a, b);
  xor xor_1 (xor_1_out, and_1_out, acc);
  and and_2 (and_2_out, and_1_out, acc);
  and and_3 (and_3_out, xor_1_out, cin);
  xor xor_2 (s, xor_1_out, cin);
  or or_1 (cout, and_2_out, and_3_out);

  assign a_out = a;
endmodule

module STEP (
  input  a,
  input  [7:0] ACCin,
  input  [7:0] b,
  output P,
  output [7:0] ACCout
);

  wire cell_1_cout, cell_2_cout, cell_3_cout, cell_4_cout, cell_5_cout, cell_6_cout, cell_7_cout;

  CELL cell_1 (.a(a), .b(b[0]), .acc(ACCin[0]), .cin(1'b0), .cout(cell_1_cout), .s(P));  // open: a_out
  CELL cell_2 (.a(a), .b(b[1]), .acc(ACCin[1]), .cin(cell_1_cout), .cout(cell_2_cout), .s(ACCout[0]));  // open: a_out
  CELL cell_3 (.a(a), .b(b[2]), .acc(ACCin[2]), .cin(cell_2_cout), .cout(cell_3_cout), .s(ACCout[1]));  // open: a_out
  CELL cell_4 (.a(a), .b(b[3]), .acc(ACCin[3]), .cin(cell_3_cout), .cout(cell_4_cout), .s(ACCout[2]));  // open: a_out
  CELL cell_5 (.a(a), .b(b[4]), .acc(ACCin[4]), .cin(cell_4_cout), .cout(cell_5_cout), .s(ACCout[3]));  // open: a_out
  CELL cell_6 (.a(a), .b(b[5]), .acc(ACCin[5]), .cin(cell_5_cout), .cout(cell_6_cout), .s(ACCout[4]));  // open: a_out
  CELL cell_7 (.a(a), .b(b[6]), .acc(ACCin[6]), .cin(cell_6_cout), .cout(cell_7_cout), .s(ACCout[5]));  // open: a_out
  CELL cell_8 (.a(a), .b(b[7]), .acc(ACCin[7]), .cin(cell_7_cout), .cout(ACCout[7]), .s(ACCout[6]));  // open: a_out
endmodule

module MULTIPLIER8 (
  input  [7:0] B,
  input  SA,
  input  SB,
  input  [7:0] A,
  output [7:0] P_HIGH,
  output [7:0] P_LOW,
  output SIGN
);

  wire or_1_out, or_2_out, xor_1_out;
  wire [7:0] step_1_accout, step_2_accout, step_3_accout, step_4_accout, step_5_accout, step_7_accout,
       step_8_accout;

  STEP step_1 (.a(A[0]), .ACCin({8{1'b0}}), .b(B), .P(P_LOW[0]), .ACCout(step_1_accout));
  STEP step_2 (.a(A[1]), .ACCin(step_1_accout), .b(B), .P(P_LOW[1]), .ACCout(step_2_accout));
  STEP step_3 (.a(A[2]), .ACCin(step_2_accout), .b(B), .P(P_LOW[2]), .ACCout(step_3_accout));
  STEP step_4 (.a(A[3]), .ACCin(step_3_accout), .b(B), .P(P_LOW[3]), .ACCout(step_4_accout));
  STEP step_5 (.a(A[5]), .ACCin(step_7_accout), .b(B), .P(P_LOW[5]), .ACCout(step_5_accout));
  STEP step_6 (.a(A[7]), .ACCin(step_8_accout), .b(B), .P(P_LOW[7]), .ACCout(P_HIGH));
  STEP step_7 (.a(A[4]), .ACCin(step_4_accout), .b(B), .P(P_LOW[4]), .ACCout(step_7_accout));
  STEP step_8 (.a(A[6]), .ACCin(step_5_accout), .b(B), .P(P_LOW[6]), .ACCout(step_8_accout));
  xor xor_1 (xor_1_out, SA, SB);
  or or_1 (or_1_out, A[0], A[1], A[2], A[3], A[4], A[5], A[6], A[7]);
  or or_2 (or_2_out, B[0], B[1], B[2], B[3], B[4], B[5], B[6], B[7]);
  and and_1 (SIGN, xor_1_out, or_1_out, or_2_out);

  // Other names for the same wires on the sheet: HI[7:0] = P_HIGH; p0 = P_LOW[0]; p1 = P_LOW[1]; p2 = P_LOW[2];
  //   p3 = P_LOW[3]; p4 = P_LOW[4]; p5 = P_LOW[5]; p6 = P_LOW[6]; p7 = P_LOW[7]
endmodule

module LOAD (
  input  Enable,
  input  [2:0] ADDR,
  input  [8:0] VALUE_IN,
  output WRITE_ACC,
  output WRITE_A,
  output WRITE_B,
  output WRITE_REM,
  output WRITE_RES,
  output [7:0] DATA_OUT,
  output SIGN_OUT
);

  Decoder #(.select(3)) decoder_1 (
    .out0(WRITE_ACC), .out1(WRITE_A), .out2(WRITE_B), .out3(WRITE_REM), .out4(WRITE_RES), .sel(ADDR),
    .en(Enable));  // open: out5, out6, out7

  assign DATA_OUT = VALUE_IN[8:1];
  assign SIGN_OUT = VALUE_IN[0];
endmodule

module Move (
  input  ENABLE,
  input  [2:0] DST,
  input  [2:0] SRC,
  input  [7:0] ACC_IN,
  input  [7:0] A_IN,
  input  [7:0] B_IN,
  input  [7:0] REM_IN,
  input  [7:0] RES_IN,
  output WRITE_ACC,
  output WRITE_A,
  output WRITE_B,
  output WRITE_REM,
  output WRITE_RES,
  output [7:0] DATA_OUT
);

  Decoder #(.select(3)) decoder_1 (
    .out0(WRITE_ACC), .out1(WRITE_A), .out2(WRITE_B), .out3(WRITE_REM), .out4(WRITE_RES), .sel(DST),
    .en(ENABLE));  // open: out5, out6, out7
  Multiplexer #(.disabled("Z"), .select(3), .width(8)) multiplexer_1 (
    .in0(ACC_IN), .in1(A_IN), .in2(B_IN), .in3(REM_IN), .in4(RES_IN), .in5({8{1'b0}}), .in6({8{1'b0}}),
    .in7({8{1'b0}}), .out(DATA_OUT), .sel(SRC));
endmodule
