// Logisim project FullSubtracter.circ as structural Verilog: 2 circuits, main circuit Full_Subtracter
module Full_Subtracter (
  input  A,
  input  B,
  input  Bin,
  output D_out_aa112aa0,
  output Borrow
);

  Multiplexer #(.enable("true"), .select(3)) multiplexer_1 (
    .in0(1'b0), .in1(1'b1), .in2(1'b1), .in3(1'b0), .in4(1'b1), .in5(1'b0), .in6(1'b0), .in7(1'b1),
    .out(D_out_aa112aa0), .sel({A, B, Bin}));  // open: en
  Multiplexer #(.enable("true"), .select(3)) multiplexer_2 (
    .in0(1'b0), .in1(1'b1), .in2(1'b1), .in3(1'b1), .in4(1'b0), .in5(1'b0), .in6(1'b0), .in7(1'b1),
    .out(Borrow), .sel({A, B, Bin}));  // open: en
endmodule

module mainFullSubtracter (
  input  [7:0] A,
  input  [7:0] B,
  output [7:0] D,
  output Borrow
);

  wire full_subtracter_1_borrow, full_subtracter_2_borrow, full_subtracter_3_borrow,
       full_subtracter_4_borrow, full_subtracter_5_borrow, full_subtracter_6_borrow, full_subtracter_7_borrow;

  Full_Subtracter full_subtracter_1 (
    .A(A[0]), .B(B[0]), .Bin(1'b0), .D_out_aa112aa0(D[0]), .Borrow(full_subtracter_1_borrow));
  Full_Subtracter full_subtracter_2 (
    .A(A[1]), .B(B[1]), .Bin(full_subtracter_1_borrow), .D_out_aa112aa0(D[1]),
    .Borrow(full_subtracter_2_borrow));
  Full_Subtracter full_subtracter_3 (
    .A(A[2]), .B(B[2]), .Bin(full_subtracter_2_borrow), .D_out_aa112aa0(D[2]),
    .Borrow(full_subtracter_3_borrow));
  Full_Subtracter full_subtracter_4 (
    .A(A[3]), .B(B[3]), .Bin(full_subtracter_3_borrow), .D_out_aa112aa0(D[3]),
    .Borrow(full_subtracter_4_borrow));
  Full_Subtracter full_subtracter_5 (
    .A(A[4]), .B(B[4]), .Bin(full_subtracter_4_borrow), .D_out_aa112aa0(D[4]),
    .Borrow(full_subtracter_5_borrow));
  Full_Subtracter full_subtracter_6 (
    .A(A[5]), .B(B[5]), .Bin(full_subtracter_5_borrow), .D_out_aa112aa0(D[5]),
    .Borrow(full_subtracter_6_borrow));
  Full_Subtracter full_subtracter_7 (
    .A(A[6]), .B(B[6]), .Bin(full_subtracter_6_borrow), .D_out_aa112aa0(D[6]),
    .Borrow(full_subtracter_7_borrow));
  Full_Subtracter full_subtracter_8 (
    .A(A[7]), .B(B[7]), .Bin(full_subtracter_7_borrow), .D_out_aa112aa0(D[7]), .Borrow(Borrow));
endmodule
