// Logisim project Move.circ as structural Verilog: 1 circuit, main circuit main
module main (
  input  MOV,
  input  [2:0] DST,
  input  [2:0] SRC,
  input  [7:0] ACC_IN,
  input  [7:0] A_IN,
  input  [7:0] B_IN,
  input  [7:0] REM_IN,
  input  [7:0] RES_IN,
  output WRITE_ACC,
  output WRITE_A,
  output WRITE_B,
  output WRITE_REM,
  output WRITE_RES,
  output [7:0] DATA_OUT
);

  Decoder #(.select(3)) decoder_1 (
    .out0(WRITE_ACC), .out1(WRITE_A), .out2(WRITE_B), .out3(WRITE_REM), .out4(WRITE_RES), .sel(DST), .en(MOV));  // open: out5, out6, out7
  Multiplexer #(.disabled("Z"), .select(3), .width(8)) multiplexer_1 (
    .in0(ACC_IN), .in1(A_IN), .in2(B_IN), .in3(REM_IN), .in4(RES_IN), .in5({8{1'b0}}), .in6({8{1'b0}}),
    .in7({8{1'b0}}), .out(DATA_OUT), .sel(SRC));
endmodule
