// Logisim project Div_8.circ as structural Verilog: 2 circuits, main circuit main
module main (
  input  [7:0] A,
  input  [7:0] B,
  output [7:0] Quotient,
  output [7:0] Reminder,
  output out_5
);

  wire comparator_1_lt, subtractor_1_bout, subtractor_2_bout, subtractor_3_bout, subtractor_4_bout,
       subtractor_5_bout, subtractor_6_bout, subtractor_7_bout, subtractor_8_bout, zero8_2_output,
       zero8_3_output, zero8_4_output, zero8_5_output, zero8_6_output, zero8_7_output, zero8_8_output,
       zero8_9_output;
  wire [2:0] pull_resistor_1_node_2;
  wire [4:0] pull_resistor_1_node;
  wire [7:0] and_8_out, multiplexer_1_out, multiplexer_2_out, multiplexer_3_out, multiplexer_4_out,
       multiplexer_6_out, multiplexer_7_out, multiplexer_8_out, subtractor_1_out, subtractor_2_out,
       subtractor_3_out, subtractor_4_out, subtractor_5_out, subtractor_6_out, subtractor_7_out,
       subtractor_8_out;

  Pull_Resistor pull_resistor_1 (.node({pull_resistor_1_node_2, pull_resistor_1_node}));
  Zero8 zero8_1 (.A(B), .Output(out_5));
  Comparator #(.mode("unsigned")) comparator_1 (.a(A), .b(B), .lt(comparator_1_lt));  // open: gt, eq
  Zero8 zero8_2 (.A({1'b0, B[7:1]}), .Output(zero8_2_output));
  Subtractor subtractor_1 (
    .a(A), .b({B[0], pull_resistor_1_node_2, pull_resistor_1_node[4:1]}), .out(subtractor_1_out),
    .bout(subtractor_1_bout));  // open: bin
  and and_1 (and_8_out[7], ~subtractor_1_bout, zero8_2_output);  // AND_Gate
  Multiplexer #(.width(8)) multiplexer_1 (.in0(A), .in1(subtractor_1_out), .out(multiplexer_1_out), .sel(and_8_out[7]));
  Subtractor subtractor_2 (
    .a(multiplexer_1_out), .b({B[1:0], pull_resistor_1_node_2, pull_resistor_1_node[4:2]}),
    .out(subtractor_2_out), .bout(subtractor_2_bout));  // open: bin
  and and_2 (and_8_out[6], ~subtractor_2_bout, zero8_3_output);  // AND_Gate
  Zero8 zero8_3 (.A({2'b00, B[7:2]}), .Output(zero8_3_output));
  Multiplexer #(.width(8)) multiplexer_2 (
    .in0(multiplexer_1_out), .in1(subtractor_2_out), .out(multiplexer_2_out), .sel(and_8_out[6]));
  Subtractor subtractor_3 (
    .a(multiplexer_2_out), .b({B[2:0], pull_resistor_1_node_2, pull_resistor_1_node[4:3]}),
    .out(subtractor_3_out), .bout(subtractor_3_bout));  // open: bin
  and and_3 (and_8_out[5], ~subtractor_3_bout, zero8_4_output);  // AND_Gate
  Zero8 zero8_4 (.A({3'b000, B[7:3]}), .Output(zero8_4_output));
  Multiplexer #(.width(8)) multiplexer_3 (
    .in0(multiplexer_2_out), .in1(subtractor_3_out), .out(multiplexer_3_out), .sel(and_8_out[5]));
  Subtractor subtractor_4 (
    .a(multiplexer_3_out), .b({B[3:0], pull_resistor_1_node_2, pull_resistor_1_node[4]}),
    .out(subtractor_4_out), .bout(subtractor_4_bout));  // open: bin
  and and_4 (and_8_out[4], ~subtractor_4_bout, zero8_5_output);  // AND_Gate
  Zero8 zero8_5 (.A({4'b0000, B[7:4]}), .Output(zero8_5_output));
  Multiplexer #(.width(8)) multiplexer_4 (
    .in0(multiplexer_3_out), .in1(subtractor_4_out), .out(multiplexer_4_out), .sel(and_8_out[4]));
  Subtractor subtractor_5 (
    .a(multiplexer_4_out), .b({B[4:0], pull_resistor_1_node_2}), .out(subtractor_5_out),
    .bout(subtractor_5_bout));  // open: bin
  and and_5 (and_8_out[3], ~subtractor_5_bout, zero8_6_output);  // AND_Gate
  Zero8 zero8_6 (.A({{5{1'b0}}, B[7:5]}), .Output(zero8_6_output));
  Multiplexer #(.width(8)) multiplexer_5 (.in0(and_8_out), .out(Quotient), .sel(comparator_1_lt));  // open: in1
  Multiplexer #(.width(8)) multiplexer_6 (
    .in0(multiplexer_4_out), .in1(subtractor_5_out), .out(multiplexer_6_out), .sel(and_8_out[3]));
  Subtractor subtractor_6 (
    .a(multiplexer_6_out), .b({B[5:0], pull_resistor_1_node_2[2:1]}), .out(subtractor_6_out),
    .bout(subtractor_6_bout));  // open: bin
  Zero8 zero8_7 (.A({{6{1'b0}}, B[7:6]}), .Output(zero8_7_output));
  and and_6 (and_8_out[2], ~subtractor_6_bout, zero8_7_output);  // AND_Gate
  Multiplexer #(.width(8)) multiplexer_7 (
    .in0(multiplexer_6_out), .in1(subtractor_6_out), .out(multiplexer_7_out), .sel(and_8_out[2]));
  Subtractor subtractor_7 (
    .a(multiplexer_7_out), .b({B[6:0], pull_resistor_1_node_2[2]}), .out(subtractor_7_out),
    .bout(subtractor_7_bout));  // open: bin
  Zero8 zero8_8 (.A({{7{1'b0}}, B[7]}), .Output(zero8_8_output));
  and and_7 (and_8_out[1], ~subtractor_7_bout, zero8_8_output);  // AND_Gate
  Multiplexer #(.width(8)) multiplexer_8 (
    .in0(multiplexer_7_out), .in1(subtractor_7_out), .out(multiplexer_8_out), .sel(and_8_out[1]));
  Zero8 zero8_9 (.A({8{1'b0}}), .Output(zero8_9_output));
  Subtractor subtractor_8 (
    .a(multiplexer_8_out), .b(B), .out(subtractor_8_out), .bout(subtractor_8_bout));  // open: bin
  and and_8 (and_8_out[0], ~subtractor_8_bout, zero8_9_output);  // AND_Gate
  Multiplexer #(.width(8)) multiplexer_9 (
    .in0(multiplexer_8_out), .in1(subtractor_8_out), .out(Reminder), .sel(and_8_out[0]));
endmodule

// Z8
module Zero8 (
  input  [7:0] A,
  output Output
);

  wire or_1_out, or_2_out, or_3_out, or_4_out, or_5_out, or_6_out;

  or or_1 (or_1_out, A[0], A[1]);
  or or_2 (or_2_out, A[2], A[3]);
  or or_3 (or_3_out, A[4], A[5]);
  or or_4 (or_4_out, A[6], A[7]);
  or or_5 (or_5_out, or_1_out, or_2_out);
  nor nor_1 (Output, or_5_out, or_6_out);
  or or_6 (or_6_out, or_3_out, or_4_out);
endmodule
