// Logisim project MULTIPLIER.circ as structural Verilog: 3 circuits, main circuit MULTIPLIER8
module CELL (
  input  a,
  input  b,
  input  acc,
  input  cin,
  output a_out,
  output cout,
  output s
);

  wire and_1_out, and_2_out, and_3_out, xor_1_out;

  and and_1 (and_1_out, a, b);
  xor xor_1 (xor_1_out, and_1_out, acc);
  and and_2 (and_2_out, and_1_out, acc);
  and and_3 (and_3_out, xor_1_out, cin);
  xor xor_2 (s, xor_1_out, cin);
  or or_1 (cout, and_2_out, and_3_out);

  assign a_out = a;
endmodule

module STEP (
  input  a,
  input  [7:0] ACCin,
  input  [7:0] b,
  output P,
  output [7:0] ACCout
);

  wire cell_1_cout, cell_2_cout, cell_3_cout, cell_4_cout, cell_5_cout, cell_6_cout, cell_7_cout;

  CELL cell_1 (.a(a), .b(b[0]), .acc(ACCin[0]), .cin(1'b0), .cout(cell_1_cout), .s(P));  // open: a_out
  CELL cell_2 (.a(a), .b(b[1]), .acc(ACCin[1]), .cin(cell_1_cout), .cout(cell_2_cout), .s(ACCout[0]));  // open: a_out
  CELL cell_3 (.a(a), .b(b[2]), .acc(ACCin[2]), .cin(cell_2_cout), .cout(cell_3_cout), .s(ACCout[1]));  // open: a_out
  CELL cell_4 (.a(a), .b(b[3]), .acc(ACCin[3]), .cin(cell_3_cout), .cout(cell_4_cout), .s(ACCout[2]));  // open: a_out
  CELL cell_5 (.a(a), .b(b[4]), .acc(ACCin[4]), .cin(cell_4_cout), .cout(cell_5_cout), .s(ACCout[3]));  // open: a_out
  CELL cell_6 (.a(a), .b(b[5]), .acc(ACCin[5]), .cin(cell_5_cout), .cout(cell_6_cout), .s(ACCout[4]));  // open: a_out
  CELL cell_7 (.a(a), .b(b[6]), .acc(ACCin[6]), .cin(cell_6_cout), .cout(cell_7_cout), .s(ACCout[5]));  // open: a_out
  CELL cell_8 (.a(a), .b(b[7]), .acc(ACCin[7]), .cin(cell_7_cout), .cout(ACCout[7]), .s(ACCout[6]));  // open: a_out
endmodule

module MULTIPLIER8 (
  input  [7:0] B,
  input  SA,
  input  SB,
  input  [7:0] A,
  output [7:0] P_HIGH,
  output [7:0] P_LOW,
  output SIGN
);

  wire or_1_out, or_2_out, xor_1_out;
  wire [7:0] step_1_accout, step_2_accout, step_3_accout, step_4_accout, step_5_accout, step_7_accout,
       step_8_accout;

  STEP step_1 (.a(A[0]), .ACCin({8{1'b0}}), .b(B), .P(P_LOW[0]), .ACCout(step_1_accout));
  STEP step_2 (.a(A[1]), .ACCin(step_1_accout), .b(B), .P(P_LOW[1]), .ACCout(step_2_accout));
  STEP step_3 (.a(A[2]), .ACCin(step_2_accout), .b(B), .P(P_LOW[2]), .ACCout(step_3_accout));
  STEP step_4 (.a(A[3]), .ACCin(step_3_accout), .b(B), .P(P_LOW[3]), .ACCout(step_4_accout));
  STEP step_5 (.a(A[5]), .ACCin(step_7_accout), .b(B), .P(P_LOW[5]), .ACCout(step_5_accout));
  STEP step_6 (.a(A[7]), .ACCin(step_8_accout), .b(B), .P(P_LOW[7]), .ACCout(P_HIGH));
  STEP step_7 (.a(A[4]), .ACCin(step_4_accout), .b(B), .P(P_LOW[4]), .ACCout(step_7_accout));
  STEP step_8 (.a(A[6]), .ACCin(step_5_accout), .b(B), .P(P_LOW[6]), .ACCout(step_8_accout));
  xor xor_1 (xor_1_out, SA, SB);
  or or_1 (or_1_out, A[0], A[1], A[2], A[3], A[4], A[5], A[6], A[7]);
  or or_2 (or_2_out, B[0], B[1], B[2], B[3], B[4], B[5], B[6], B[7]);
  and and_1 (SIGN, xor_1_out, or_1_out, or_2_out);

  // Other names for the same wires on the sheet: HI[7:0] = P_HIGH; p0 = P_LOW[0]; p1 = P_LOW[1]; p2 = P_LOW[2];
  //   p3 = P_LOW[3]; p4 = P_LOW[4]; p5 = P_LOW[5]; p6 = P_LOW[6]; p7 = P_LOW[7]
endmodule
