// Logisim project register.circ as structural Verilog: 2 circuits, main circuit registor
module registor (
  input  CLOCK,
  input  WRITE,
  input  I0,
  input  I1,
  input  I2,
  input  I3,
  input  I4,
  input  I5,
  input  I6,
  input  I7,
  output B0,
  output B1,
  output B2,
  output B3,
  output B4,
  output B5,
  output B6,
  output B7
);

  Dflipflop C1 (.CLOCK(CLOCK), .Write(WRITE), .D(I0), .val(B0));
  Dflipflop C2 (.CLOCK(CLOCK), .Write(WRITE), .D(I1), .val(B1));
  Dflipflop C3 (.CLOCK(CLOCK), .Write(WRITE), .D(I2), .val(B2));
  Dflipflop C4 (.CLOCK(CLOCK), .Write(WRITE), .D(I3), .val(B3));
  Dflipflop C5 (.CLOCK(CLOCK), .Write(WRITE), .D(I4), .val(B4));
  Dflipflop C6 (.CLOCK(CLOCK), .Write(WRITE), .D(I5), .val(B5));
  Dflipflop C7 (.CLOCK(CLOCK), .Write(WRITE), .D(I6), .val(B6));
  Dflipflop C8 (.CLOCK(CLOCK), .Write(WRITE), .D(I7), .val(B7));
endmodule

module Dflipflop (
  input  CLOCK,
  input  Write,
  input  D,
  output val
);

  wire and_1_out, nand_2_out, not_1_out, R_out, S_out;

  and and_1 (and_1_out, CLOCK, Write);
  not not_1 (not_1_out, D);
  nand S (S_out, D, and_1_out);
  nand R (R_out, and_1_out, not_1_out);
  nand nand_1 (val, S_out, nand_2_out);
  nand nand_2 (nand_2_out, val, R_out);
endmodule
