// Logisim project register.circ as structural Verilog: 2 circuits, main circuit registor
module registor (
  input  CLOCK,
  input  WRITE,
  input  I0,
  input  I1,
  input  I2,
  input  I3,
  input  I4,
  input  I5,
  input  I6,
  input  I7,
  output out_11,
  output out_12
);

  Dflipflop C1 (.CLOCK(CLOCK), .Write(WRITE), .D(I0), .val(out_11));
  Dflipflop C2 (.CLOCK(CLOCK), .Write(WRITE), .D(I1), .val(out_12));
  Dflipflop C3 (.CLOCK(CLOCK), .Write(WRITE), .D(I2));  // open: val
  Dflipflop C4 (.CLOCK(CLOCK), .Write(WRITE), .D(I3));  // open: val
  Dflipflop C5 (.CLOCK(CLOCK), .Write(WRITE), .D(I4));  // open: val
  Dflipflop C6 (.CLOCK(CLOCK), .Write(WRITE), .D(I5));  // open: val
  Dflipflop C7 (.CLOCK(CLOCK), .Write(WRITE), .D(I6));  // open: val
  Dflipflop C8 (.CLOCK(CLOCK), .Write(WRITE), .D(I7));  // open: val
endmodule

module Dflipflop (
  input  CLOCK,
  input  Write,
  input  D,
  output val
);

  wire and_1_out, nand_2_out, not_1_out, R_out, S_out;

  and and_1 (and_1_out, CLOCK, Write);
  not not_1 (not_1_out, D);
  nand S (S_out, D, and_1_out);
  nand R (R_out, and_1_out, not_1_out);
  nand nand_1 (val, S_out, nand_2_out);
  nand nand_2 (nand_2_out, val, R_out);
endmodule
